# Fritzing sketch 2 LCD (saved by Fritzing 0.9.3b)

parts:
  Componente1 = Arduino Sensor Shield v5.0
  Componente2 = LCD1602-I2C

nets:
  GND: Componente1.GND, Componente2.GND
  +5V: Componente1.+5V, Componente1.SCL, Componente2.VCC, Componente2.SCL
  N1: Componente1.SDA, Componente2.SDA

notes:
  LCD
  + <-> Vcc
  - <-> GND
  SDA <-> SDA
  SCL <-> SCL

custom parts:
  LCD1602-I2C: A standard character display, usually with 2x16 characters. Comes in many colors with LCM1602 IIC attached.
