# Fritzing sketch 3 Meteo BME280 (saved by Fritzing 0.9.3b)

parts:
  Componente1 = Arduino Sensor Shield v5.0
  Componente2 = LCD1602-I2C
  BMP280_Breakout1 = BMP280 Breakout Board [part_number=BMP280]

nets:
  N1: Componente1.A4, BMP280_Breakout1.SDA
  N2: Componente1.A5, BMP280_Breakout1.SCL
  N3: Componente1.GND#38, Componente2.GND
  N4: Componente1.+5V#65, Componente1.SCL, Componente2.VCC, Componente2.SCL
  N5: Componente1.SDA, Componente2.SDA
  N6: Componente1.GND#137, BMP280_Breakout1.GND
  N7: Componente1.+5V#143, BMP280_Breakout1.VCC

notes:
  LCD
  + <-> Vcc
  - <-> GND
  SDA <-> SDA
  SCL <-> SCL
  BME280
  V <-> Vcc
  G <->GND
  A4 <-> SDA
  A5 <-> SCL

custom parts:
  LCD1602-I2C: A standard character display, usually with 2x16 characters. Comes in many colors with LCM1602 IIC attached.
  BMP280 Breakout Board: This is a breakout board for the Bosch Sensortec BMP280, "an absolute barometric pressure sensor especially designed for mobile applications." The operation range is 300 to 1100 hPa. Supply voltage is 1.2 to 3.6V. Operating temperature range is -40 to +85 °C.
