# Fritzing sketch Comparando temperaturas (saved by Fritzing 0.9.3b)

parts:
  Componente1 = Arduino Sensor Shield v5.0
  DHT1 = DHT22 Humidity and Temperature Sensor
  DHT2 = DHT22 Humidity and Temperature Sensor

nets:
  N1: Componente1.+5V#55, DHT1.VDD
  N2: Componente1.D4, DHT2.DATA
  N3: Componente1.D6, DHT1.DATA
  N4: Componente1.+5V#90, DHT2.VDD
  N5: Componente1.GND#96, DHT1.GND
  N6: Componente1.GND#144, DHT2.GND
