# Fritzing sketch Control Ventilacion (saved by Fritzing 0.9.3b)

parts:
  Componente1 = Arduino Sensor Shield v5.0
  J1 = Basic Servo
  DHT1 = DHT22 Humidity and Temperature Sensor
  DHT2 = DHT22 Humidity and Temperature Sensor

nets:
  N1: Componente1.+5V#52, Componente1.+5V#108, J1.vcc
  GND: Componente1.GND#53, Componente1.GND#96, Componente1.GND#123, J1.gnd, DHT1.GND
  N2: Componente1.+5V#55, DHT1.VDD
  N3: Componente1.D8, J1.pulse
  N4: Componente1.D4, DHT2.DATA
  N5: Componente1.D6, DHT1.DATA
  N6: Componente1.+5V#90, DHT2.VDD
  N7: Componente1.GND#144, DHT2.GND
