# Fritzing sketch Control_iluminacion (saved by Fritzing 0.9.3b)

parts:
  Componente1 = Arduino Sensor Shield v5.0
  LED1 = RGB LED - (4 legs) [package="5 mm [THT]"]
  Componente2 = Ambient Light Sensor (TEMT6000 Breakout Board)
  R1 = Rotary Potentiometer (Large) [maximum_resistance=100kΩ package=THT]

nets:
  N1: Componente1.A0, R1.wiper
  N2: Componente1.A2, Componente2.S
  N3: Componente1.GND#53, Componente1.GND#118, LED1.common_anode
  N4: Componente1.D13, LED1.green_cathode
  N5: Componente1.GND#132, R1.leg2
  N6: Componente1.GND#134, Componente2.GND
  N7: Componente1.+5V#138, R1.leg1
  N8: Componente1.+5V#140, Componente2.VCC
